# Fritzing sketch doorbell-rec (saved by Fritzing 0.9.2b)

parts:
  Raspberry_Pi1 = Raspberry Pi 2
  Part1 = Arduino Pro Mini v13
  U1 = mystery part, 3 pins [chip_label=?]

nets:
  3V3: Raspberry_Pi1.3v3, Raspberry_Pi1.3V3, Part1.VCC, U1.pin1
  GND: Raspberry_Pi1.GND, Part1.GND, U1.pin3
  N1: Raspberry_Pi1.GPIO15, Part1.D0/TX
  N2: Raspberry_Pi1.GPIO14, Part1.D1/RX
  N3: Part1.D2, U1.pin2

notes:
  433Mhz Receiver
